# Fritzing sketch RaspBEERyPi (saved by Fritzing 0.7.4b)
breadboards: 1

parts:
  IC1 = IC, DIP package, 16 pins [chip_label=MCP3008 spacing=300mil]
  T1 = TMP36 Temperature Sensor [package="TO92 [THT]"]
  Pi1 = Adafruit Pi Cobbler

nets:
  GND: IC1.pin1, IC1.pin6, T1.GND, Pi1.GND
  N1: IC1.pin2, Pi1.#25
  N2: IC1.pin3, Pi1.#24
  N3: IC1.pin4, Pi1.#23
  N4: IC1.pin5, Pi1.#18
  N5: IC1.pin7, IC1.pin8, T1.+Vs, Pi1.3V3
  N6: IC1.pin16, T1.Vout

custom parts:
  Adafruit Pi Cobbler: Adafruit Pi Cobbler GPIO Breakout for Raspberry Pi
